# Fritzing sketch Project2-Circuit-Diagram (saved by Fritzing 0.9.3b)

parts:
  R1 = BBC MicroBit
  R2 = Rotary Potentiometer (Small) [maximum_resistance=100kΩ package=THT]
  LED1 = LED - 5mm [color="Red (633nm)" package="5 mm [THT]"]

nets:
  N1: R1.GND, R2.leg2, LED1.cathode
  N2: R1.3v3, R2.leg1
  N3: R1.P1_ANALOG_IN, LED1.anode
  N4: R1.P0_ANALOG_IN, R2.wiper

custom parts:
  BBC MicroBit: The BBC MICRO:BIT
